# Fritzing sketch Schema (saved by Fritzing 0.9.3b)
breadboards: 2

parts:
  R2 = Resistor [tolerance=±5% resistance=10k package="1206 [SMD]"]
  S2 = Toggle Switch [package=THT]
  U1 = LIPO-1000mAh [package=lipo-1000]
  U2 = NodeMCU V1.0
  R3 = Rotary Potentiometer (Small) [maximum_resistance=100kΩ package=THT]
  R4 = Resistor [tolerance=±5% resistance=100 package="1206 [SMD]"]
  LED1 = smd LED [color="Red (633nm)" package="0805 [SMD]"]
  MCP1700-3302E/TO = Voltage Regulator [package=to-92]

nets:
  N1: R2.Pin_0, S2.COM, U2.GND, R3.wiper, LED1.cathode
  N2: R2.Pin_1, U2.D8
  N3: S2.L2, U1.-
  N4: U1.+, MCP1700-3302E/TO.IN
  N5: U2.3V3, MCP1700-3302E/TO.OUT
  N6: U2.D5, R3.leg1
  N7: U2.D6, R3.leg2
  N8: U2.D7, R4.Pin_0
  N9: R4.Pin_1, LED1.anode

custom parts:
  NodeMCU V1.0: ESP8266 based NodeMCU
