# Fritzing sketch Schema_wemos (saved by Fritzing 0.9.3b)
breadboards: 1

parts:
  S1 = Square Pushbutton
  LED1 = smd LED [color="Green (565nm)" package="1206 [SMD]"]
  WeMos_D1_Mini1 = WeMos D1 Mini
  R2 = Resistor [tolerance=±5% resistance=10k package="1206 [SMD]"]
  S2 = Toggle Switch [package=THT]
  U1 = LIPO-1000mAh [package=lipo-1000]
  RE1 = Rotary Encoder [package=THT]
  S3 = Pushbutton [package="[THT]"]
  R3 = Resistor [tolerance=±5% resistance=10k package="1206 [SMD]"]
  R4 = Resistor [tolerance=±5% resistance=22k package=THT]
  R5 = Resistor [tolerance=±5% resistance=22k package=THT]

nets:
  N1: S1.leg0, WeMos_D1_Mini1.RST, R3.Pin_0
  N2: S1.leg1, LED1.cathode, WeMos_D1_Mini1.G, R2.Pin_1, S2.COM, RE1.EncoderPinC, R5.Pin_1
  N3: LED1.anode, WeMos_D1_Mini1.D7
  N4: WeMos_D1_Mini1.3V3, S3.Pin_1, S3.Pin_2, R3.Pin_1
  N5: WeMos_D1_Mini1.5V, U1.+, R4.Pin_1
  N6: WeMos_D1_Mini1.A0, R4.Pin_0, R5.Pin_0
  N7: WeMos_D1_Mini1.D5, RE1.EncoderPinA
  N8: WeMos_D1_Mini1.D6, RE1.EncoderPinB
  N9: WeMos_D1_Mini1.D8, R2.Pin_0, S3.Pin_3, S3.Pin_4
  N10: S2.L1, U1.-
